# Fritzing sketch BrotherLink (saved by Fritzing 0.9.2b)
breadboards: 1

parts:
  WeMos_D1_Mini1 = WeMos D1 Mini
  Часть2 = Logic Level Converter
  Часть1 = Breadboard Power Supply Board SMD
  KH-9xx_Port = shrouded pin header, 8 pins [form="♂ (shrouded male)"]
  S1 = Reed switch [package=THT]
  R1 = Resistor [tolerance=±5% resistance=10k package=THT]

nets:
  N1: WeMos_D1_Mini1.3V3, Часть2.LV, S1.pin_2
  GND: WeMos_D1_Mini1.G, Часть2.GND, Часть1.GND, KH-9xx_Port.pin1, R1.Pin_0
  N2: WeMos_D1_Mini1.RX, Часть2.TX_LV
  N3: WeMos_D1_Mini1.TX, Часть2.RX_LV
  N4: Часть2.TX_HV, KH-9xx_Port.pin4
  N5: Часть2.RX_HV, KH-9xx_Port.pin6
  N6: Часть2.HV, Часть1.VCC, KH-9xx_Port.pin2
  N7: S1.pin_1, R1.Pin_1

notes:
  +5V
  +3.3V

custom parts:
  WeMos D1 Mini: The D1 mini is a mini wifi board based on ESP-8266EX.
